# Fritzing sketch postbox (saved by Fritzing 0.9.3b)

parts:
  Part1 = Arduino Nano (Rev3.0)
  LED1 = LED - 5mm [color="Red (633nm)" package="5 mm [THT]"]
  S1 = Pushbutton [package=THT]
  Barrel_Plug = Power plug
  LED2 = smd LED [color="Green (565nm)" package="0805 [SMD]"]
  D1 = Rectifier Diode [part_number=1N4001 package="300 mil [THT]"]
  R1 = Resistor [tolerance=±5% resistance=220 package=THT]
  R2 = Resistor [tolerance=±5% resistance=220 package=THT]
  R3 = Resistor [tolerance=±5% resistance=10k package=THT]

nets:
  GND: Part1.GND, Barrel_Plug.GND, R1.Pin_1, R2.Pin_1, R3.Pin_0
  N1: Part1.D2, S1.leg1, R3.Pin_1
  N2: Part1.D3, LED1.anode
  N3: Part1.D4, LED2.anode
  N4: Part1.VIN, D1.cathode
  N5: Part1.3V3, S1.leg0
  N6: LED1.cathode, R2.Pin_0
  N7: Barrel_Plug.VCC, D1.anode
  N8: LED2.cathode, R1.Pin_0
